// Logisim project 1911870642_Md.Mehedi_Hasan_Bhuiyan_Nipu.circ as structural Verilog: 4 circuits, main circuit Register file
module Register_file (
  input  [3:0] Read_reg1,
  input  [3:0] WriteReg,
  input  [3:0] ReadReg_2,
  input  [15:0] Write_Data,
  input  Write_EN,
  input  Clock,
  output [15:0] Read_data_1,
  output [15:0] Read_data_2
);

  wire and_1_out, and_2_out, and_3_out, and_4_out, and_5_out, and_6_out, and_7_out, and_8_out, and_9_out,
       and_10_out, and_11_out, and_12_out, and_13_out, and_14_out, and_15_out, and_16_out, decoder_1_out0,
       decoder_1_out1, decoder_1_out2, decoder_1_out3, decoder_1_out4, decoder_1_out5, decoder_1_out6,
       decoder_1_out7, decoder_1_out8, decoder_1_out9, decoder_1_out10, decoder_1_out11, decoder_1_out12,
       decoder_1_out13, decoder_1_out14, decoder_1_out15;
  wire [15:0] register_1_q, register_2_q, register_3_q, register_4_q, register_5_q, register_6_q,
       register_7_q, register_8_q, register_9_q, register_10_q, register_11_q, register_12_q, register_13_q,
       register_14_q, register_15_q, register_16_q;

  Decoder #(.select(4)) decoder_1 (
    .out0(decoder_1_out0), .out1(decoder_1_out1), .out2(decoder_1_out2), .out3(decoder_1_out3),
    .out4(decoder_1_out4), .out5(decoder_1_out5), .out6(decoder_1_out6), .out7(decoder_1_out7),
    .out8(decoder_1_out8), .out9(decoder_1_out9), .out10(decoder_1_out10), .out11(decoder_1_out11),
    .out12(decoder_1_out12), .out13(decoder_1_out13), .out14(decoder_1_out14), .out15(decoder_1_out15),
    .sel(WriteReg));  // open: en
  and and_1 (and_1_out, decoder_1_out0, Write_EN);
  and and_2 (and_2_out, decoder_1_out1, Write_EN);
  and and_3 (and_3_out, decoder_1_out2, Write_EN);
  and and_4 (and_4_out, decoder_1_out3, Write_EN);
  and and_5 (and_5_out, decoder_1_out4, Write_EN);
  and and_6 (and_6_out, decoder_1_out5, Write_EN);
  and and_7 (and_7_out, decoder_1_out6, Write_EN);
  and and_8 (and_8_out, decoder_1_out8, Write_EN);
  and and_9 (and_9_out, decoder_1_out9, Write_EN);
  and and_10 (and_10_out, decoder_1_out10, Write_EN);
  and and_11 (and_11_out, decoder_1_out11, Write_EN);
  and and_12 (and_12_out, decoder_1_out12, Write_EN);
  and and_13 (and_13_out, decoder_1_out13, Write_EN);
  and and_14 (and_14_out, decoder_1_out14, Write_EN);
  and and_15 (and_15_out, decoder_1_out15, Write_EN);
  Register #(.width(16)) register_1 (.D(Write_Data), .en(and_1_out), .Q(register_1_q), .clk(Clock));  // open: clr
  Register #(.width(16)) register_2 (.D(Write_Data), .en(and_2_out), .Q(register_2_q), .clk(Clock));  // open: clr
  Register #(.width(16)) register_3 (.D(Write_Data), .en(and_3_out), .Q(register_3_q), .clk(Clock));  // open: clr
  Register #(.width(16)) register_4 (.D(Write_Data), .en(and_4_out), .Q(register_4_q), .clk(Clock));  // open: clr
  Register #(.width(16)) register_5 (.D(Write_Data), .en(and_5_out), .Q(register_5_q), .clk(Clock));  // open: clr
  Register #(.width(16)) register_6 (.D(Write_Data), .en(and_6_out), .Q(register_6_q), .clk(Clock));  // open: clr
  Register #(.width(16)) register_7 (.D(Write_Data), .en(and_7_out), .Q(register_7_q), .clk(Clock));  // open: clr
  Register #(.width(16)) register_8 (.D(Write_Data), .en(and_16_out), .Q(register_8_q), .clk(Clock));  // open: clr
  and and_16 (and_16_out, decoder_1_out7, Write_EN);
  Register #(.width(16)) register_9 (.D(Write_Data), .en(and_8_out), .Q(register_9_q), .clk(Clock));  // open: clr
  Register #(.width(16)) register_10 (.D(Write_Data), .en(and_9_out), .Q(register_10_q), .clk(Clock));  // open: clr
  Register #(.width(16)) register_11 (.D(Write_Data), .en(and_10_out), .Q(register_11_q), .clk(Clock));  // open: clr
  Register #(.width(16)) register_12 (.D(Write_Data), .en(and_11_out), .Q(register_12_q), .clk(Clock));  // open: clr
  Register #(.width(16)) register_13 (.D(Write_Data), .en(and_12_out), .Q(register_13_q), .clk(Clock));  // open: clr
  Register #(.width(16)) register_14 (.D(Write_Data), .en(and_13_out), .Q(register_14_q), .clk(Clock));  // open: clr
  Register #(.width(16)) register_15 (.D(Write_Data), .en(and_14_out), .Q(register_15_q), .clk(Clock));  // open: clr
  Register #(.width(16)) register_16 (.D(Write_Data), .en(and_15_out), .Q(register_16_q), .clk(Clock));  // open: clr
  Multiplexer #(.select(4), .width(16)) multiplexer_1 (
    .in0(register_1_q), .in1(register_2_q), .in2(register_3_q), .in3(register_4_q), .in4(register_5_q),
    .in5(register_6_q), .in6(register_7_q), .in7(register_8_q), .in8(register_9_q), .in9(register_10_q),
    .in10(register_11_q), .in11(register_12_q), .in12(register_13_q), .in13(register_14_q),
    .in14(register_15_q), .in15(register_16_q), .out(Read_data_1), .sel(Read_reg1));  // open: en
  Multiplexer #(.select(4), .width(16)) multiplexer_2 (
    .in0(register_1_q), .in1(register_2_q), .in2(register_3_q), .in3(register_4_q), .in4(register_5_q),
    .in5(register_6_q), .in6(register_7_q), .in7(register_8_q), .in8(register_9_q), .in9(register_10_q),
    .in10(register_11_q), .in11(register_12_q), .in12(register_13_q), .in13(register_14_q),
    .in14(register_15_q), .in15(register_16_q), .out(Read_data_2), .sel(ReadReg_2));  // open: en
endmodule

module ALU (
  input  [15:0] in_1,
  input  [15:0] in_2,
  input  Cin,
  input  [2:0] ALUOP,
  input  Binv,
  output [15:0] Result,
  output Cout,
  output zero
);

  wire comparator_1_lt;
  wire [3:0] bit_extender_1_out;
  wire [15:0] adder_1_out, and_1_out, bit_extender_2_out, multiplexer_1_out, not_1_out, shifter_1_out;

  assign not_1_out = ~in_2;  // NOT_Gate not_1, 16 bits wide
  Multiplexer #(.width(16), .enable("false")) multiplexer_1 (
    .in0(in_2), .in1(not_1_out), .out(multiplexer_1_out), .sel(Binv));
  Bit_Extender #(.in_width(16), .out_width(4)) bit_extender_1 (.in(in_2), .out(bit_extender_1_out));
  Comparator #(.width(16)) comparator_1 (.a(in_1), .b(in_2), .lt(comparator_1_lt));  // open: gt, eq
  assign and_1_out = in_1 & in_2;  // AND_Gate and_1, 16 bits wide
  Adder #(.width(16)) adder_1 (.a(in_1), .b(multiplexer_1_out), .out(adder_1_out), .cin(Cin), .cout(Cout));
  Shifter #(.width(16)) shifter_1 (.in(in_1), .\dist (bit_extender_1_out), .out(shifter_1_out));
  assign bit_extender_2_out = {{15{1'b0}}, comparator_1_lt};  // Bit_Extender bit_extender_2
  Multiplexer #(.select(3), .width(16), .enable("false")) multiplexer_2 (
    .in0(bit_extender_2_out), .in1(and_1_out), .in2(adder_1_out), .in3(shifter_1_out), .out(Result),
    .sel(ALUOP));  // open: in4, in5, in6, in7
  nor nor_1 (zero, Result[0], Result[1], Result[2], Result[3], Result[4], Result[5], Result[6], Result[7], Result[8], Result[9], Result[10], Result[11], Result[12], Result[13], Result[14], Result[15]);

  // Notes on the sheet:
  //   A
  //   B
endmodule

module Control_Unit (
  input  [3:0] in_1,
  output Cin,
  output Binv,
  output RT___RD,
  output RD___IM,
  output Branch,
  output [2:0] ALUop,
  output WriteEN,
  output RAMSelect,
  output MemRead,
  output MemWrite,
  output MemToRegister
);

  wire decoder_1_out0, decoder_1_out1, decoder_1_out2, decoder_1_out3, decoder_1_out4, decoder_1_out8,
       decoder_1_out9, decoder_1_out10, decoder_1_out11, decoder_1_out12, decoder_1_out13, decoder_1_out14,
       decoder_1_out15;

  Decoder #(.select(4), .enable("false")) decoder_1 (
    .out0(decoder_1_out0), .out1(decoder_1_out1), .out2(decoder_1_out2), .out3(decoder_1_out3),
    .out4(decoder_1_out4), .out5(MemWrite), .out6(Binv), .out7(MemRead), .out8(decoder_1_out8),
    .out9(decoder_1_out9), .out10(decoder_1_out10), .out11(decoder_1_out11), .out12(decoder_1_out12),
    .out13(decoder_1_out13), .out14(decoder_1_out14), .out15(decoder_1_out15), .sel(in_1));
  or or_1 (RT___RD, decoder_1_out2, decoder_1_out3, decoder_1_out4, Binv, decoder_1_out9);
  or or_2 (RD___IM, decoder_1_out1, MemWrite, MemRead, decoder_1_out8, decoder_1_out10);
  or or_3 (Branch, decoder_1_out1, decoder_1_out10);
  or or_4 (ALUop[0], decoder_1_out3, decoder_1_out9);
  or or_5 (ALUop[1], decoder_1_out4, MemWrite, Binv, MemRead, decoder_1_out8, decoder_1_out9, decoder_1_out10);
  or or_6 (RAMSelect, MemWrite, MemRead);
  or or_7 (MemToRegister, MemWrite, MemRead);
  or or_8 (WriteEN, decoder_1_out3, decoder_1_out4, Binv, MemRead, decoder_1_out8, decoder_1_out9);

  assign ALUop[2] = 1'b0;
  assign Cin = Binv;
endmodule

module Datapath (
  output [3:0] Rs,
  output [15:0] A,
  output [3:0] RT,
  output [15:0] B,
  output [3:0] RD,
  output out_6,
  output Cout,
  output [15:0] out_8,
  output [15:0] out_9
);

  wire and_1_out, clock_1_out, control_unit_1_binv, control_unit_1_branch, control_unit_1_cin,
       control_unit_1_memread, control_unit_1_memtoregister, control_unit_1_memwrite,
       control_unit_1_ramselect, control_unit_1_rd___im, control_unit_1_rt___rd, control_unit_1_writeen;
  wire [2:0] control_unit_1_aluop;
  wire [3:0] multiplexer_1_out;
  wire [15:0] adder_1_out, alu_1_result, bit_extender_1_out, multiplexer_3_out, ram_1_data, register_1_q;
  wire [15:12] rom_1_data;

  Clock clock_1 (.out(clock_1_out));
  Register #(.width(16)) register_1 (.D(multiplexer_3_out), .Q(register_1_q), .clk(clock_1_out));  // open: en, clr
  Adder #(.width(16)) adder_1 (.a(16'h1), .b(register_1_q), .out(adder_1_out));  // open: cin, cout
  ROM #(.addrWidth(16), .dataWidth(16)) rom_1 (.addr(register_1_q), .data({rom_1_data, Rs, RT, RD}));  // open: sel
  Control_Unit control_unit_1 (
    .in_1(rom_1_data), .Cin(control_unit_1_cin), .Binv(control_unit_1_binv),
    .RT___RD(control_unit_1_rt___rd), .RD___IM(control_unit_1_rd___im), .Branch(control_unit_1_branch),
    .ALUop(control_unit_1_aluop), .WriteEN(control_unit_1_writeen), .RAMSelect(control_unit_1_ramselect),
    .MemRead(control_unit_1_memread), .MemWrite(control_unit_1_memwrite),
    .MemToRegister(control_unit_1_memtoregister));
  Multiplexer #(.width(4), .enable("false")) multiplexer_1 (
    .in0(RT), .in1(RD), .out(multiplexer_1_out), .sel(control_unit_1_rt___rd));
  assign bit_extender_1_out = {{12{1'b0}}, Rs};  // Bit_Extender bit_extender_1
  Register_file register_file_1 (
    .Write_Data(out_9), .Read_data_1(A), .Read_data_2(B), .WriteReg(multiplexer_1_out), .Read_reg1(Rs),
    .ReadReg_2(RT), .Write_EN(control_unit_1_writeen), .Clock(clock_1_out));
  Multiplexer #(.width(16), .enable("false")) multiplexer_2 (
    .in0(B), .in1(bit_extender_1_out), .out(out_8), .sel(control_unit_1_rd___im));
  ALU alu_1 (
    .in_1(A), .in_2(out_8), .Cin(control_unit_1_cin), .ALUOP(control_unit_1_aluop),
    .Binv(control_unit_1_binv), .Result(alu_1_result), .Cout(Cout), .zero(out_6));
  and and_1 (and_1_out, control_unit_1_branch, out_6);
  RAM #(.addrWidth(16), .dataWidth(16), .bus("separate")) ram_1 (
    .addr(alu_1_result), .data(ram_1_data), .str(control_unit_1_memwrite), .sel(control_unit_1_ramselect),
    .clk(clock_1_out), .ld(control_unit_1_memread));  // open: din, clr
  Multiplexer #(.width(16), .enable("false")) multiplexer_3 (
    .in0(adder_1_out), .in1(bit_extender_1_out), .out(multiplexer_3_out), .sel(and_1_out));
  Multiplexer #(.width(16), .enable("false")) multiplexer_4 (
    .in0(alu_1_result), .in1(ram_1_data), .out(out_9), .sel(control_unit_1_memtoregister));
endmodule
